# Fritzing sketch batterieControler (saved by Fritzing 0.9.2b)
breadboards: 1

parts:
  IC1 = LM3914/5/6 [package=THT]
  Raspberry_Pi1 = Raspberry Pi 2  # not connected
  U1 = BATTERY-2 [package=battery-aa]

nets:
  N1: IC1.V-, U1.-1
  N2: IC1.V+, U1.+1

custom parts:
  LM3914/5/6: LM3914, LM3915, and LM3916 Dot/Bar Display Drivers Analog signal in turns on up to 10 LEDs.
