# Fritzing sketch ADconvertor (saved by Fritzing 0.9.2b)
circuit board: 6.5cm x 5.6cm
breadboards: 1

parts:
  in = screw terminal, 8 pins
  out = screw terminal, 8 pins
  MCP3008 = MCP3008 8-channel 10-bit ADC [part_number=MCP3008]

nets:
  N1: in.pin1, MCP3008.CH7
  N2: in.pin2, MCP3008.CH6
  N3: in.pin3, MCP3008.CH5
  N4: in.pin4, MCP3008.CH4
  N5: in.pin5, MCP3008.CH3
  N6: in.pin6, MCP3008.CH2
  N7: in.pin7, MCP3008.CH1
  N8: in.pin8, MCP3008.CH0
  N9: out.pin1, MCP3008.Vref, MCP3008.Vdd
  N10: out.pin2, MCP3008.DGND, MCP3008.AGND
  N11: out.pin3, MCP3008.CLK
  N12: out.pin4, MCP3008.Dout
  N13: out.pin5, MCP3008.Din
  N14: out.pin6, MCP3008.CS

notes:
  +3.3 v
  gnd
  spi:cs
  spi:in
  spi:out
  spi:clk
  +3.3V
  Jouke Hijlkema 2016
