# Fritzing sketch Powermanager (saved by Fritzing 0.9.2b)
circuit board: 5cm x 5.6cm
breadboards: 1

parts:
  10k = Resistor [tolerance=±5% resistance=10k package=THT]
  120k = Resistor [tolerance=±5% resistance=120k package=THT]
  10k_2 = Trimmer Potentiometer [maximum_resistance=10kΩ package=THT]
  56k = Resistor [tolerance=±5% resistance=56k package=THT]
  10k_3 = Resistor [tolerance=±5% resistance=10k package=THT]
  f|h|e = male pin header, 3 pins [form="♂ (male)"]
  10k_4 = Resistor [tolerance=±5% resistance=10k package=THT]
  IC1 = LM3914/5/6 [package=THT]
  47k = Resistor [tolerance=±5% resistance=47k package=THT]
  LD1117_3_3v = V_REG_LD1117VXX [package=78xxl]
  78005_5V = Voltage Regulator [package=to-220-alt]
  gnd|3_3|5 = male pin header, 3 pins [form="♂ (male)"]
  78005_5V1 = Voltage Regulator [package=to-220-alt]
  3k9 = Resistor [tolerance=±5% resistance=3.9k package=THT]
  gnd|5 = male pin header, 2 pins [form="♂ (male)"]
  12|gnd = double row male pin header, 2 pins [form="♂ (male)"]

nets:
  N1: 10k.Pin_0, 10k_3.Pin_1, 10k_4.Pin_1, LD1117_3_3v.OUT, gnd|3_3|5.pin2
  N2: 10k.Pin_1, f|h|e.pin1, IC1.LED10
  N3: 120k.Pin_0, IC1.R-LO
  N4: 120k.Pin_1, 47k.Pin_0
  N5: 10k_2.leg1, 56k.Pin_1
  N6: 10k_2.wiper, IC1.SIG
  GND: 10k_2.leg2, IC1.V-, IC1.REF_ADJ, 47k.Pin_1, LD1117_3_3v.GND, 78005_5V.GND, gnd|3_3|5.pin1, 78005_5V1.GND, 3k9.Pin_1, gnd|5.pin2, 12|gnd.pin1
  N7: 56k.Pin_0, IC1.V+, IC1.Mode, LD1117_3_3v.IN, 78005_5V.IN, 78005_5V1.IN, 12|gnd.pin2
  N8: 10k_3.Pin_0, f|h|e.pin3, IC1.LED2
  N9: f|h|e.pin2, 10k_4.Pin_0, IC1.LED6
  N10: IC1.R-HI, IC1.REF_OUT, 3k9.Pin_0
  N11: 78005_5V.OUT, gnd|3_3|5.pin3
  N12: 78005_5V1.OUT, gnd|5.pin1

notes:
  out
  in
  bat

custom parts:
  LM3914/5/6: LM3914, LM3915, and LM3916 Dot/Bar Display Drivers Analog signal in turns on up to 10 LEDs.
